# Fritzing sketch Esp_Mad_v1.0 (saved by Fritzing 0.9.3b)
circuit board: 5.5cm x 5.5cm
breadboards: 1

parts:
  ESP32_Lolin_Lite = Wemos Lolin32lite
  MPU_6050 = MPU-6050 Board GY-521 [form="♀ (female)" package=THT]
  TP1 = TP4056 [chip_label=TP4056 package="DIP (Dual Inline) [THT]"]  # not connected

nets:
  N1: ESP32_Lolin_Lite.pin_13, MPU_6050.pin2
  N2: ESP32_Lolin_Lite.pin_25, MPU_6050.pin4
  N3: ESP32_Lolin_Lite.pin_26, MPU_6050.pin3
  N4: ESP32_Lolin_Lite.pin_28, MPU_6050.pin1

notes:
  ESP-MAD V1.0 - Aneg 2019

custom parts:
  Wemos Lolin32lite: Wemos Lolinlite32 wifi and blue tooth board based on the ESP-32 cpu, digital I/Os 19, analog inputs 6, clock 240mhz, Flash 4Mbytes, lipo battery charger (500ma connection broken out on breadboard but not pcb), usb.
  MPU-6050 Board GY-521: Acelerometro y Giroscopio MPU-6050 Board GY-521
  TP4056: A DIP stand-in part for whatever IC you want. With 6 pins on a 300mil dual inline package (DIP) footprint.
