# Fritzing sketch Esp_Mad_V1.1-CarteMCU (saved by Fritzing 0.9.3b)
circuit board: 3.5cm x 5.5cm
breadboards: 1

parts:
  ESP32_Lolin_Lite = Wemos Lolin32lite
  J1 = female pin header, 4 pins [form="♀ (female)"]

nets:
  N1: ESP32_Lolin_Lite.pin_13, J1.pin1
  N2: ESP32_Lolin_Lite.pin_25, J1.pin4
  N3: ESP32_Lolin_Lite.pin_26, J1.pin3
  N4: ESP32_Lolin_Lite.pin_28, J1.pin2

notes:
  ESP-MAD V1.1 - Aneg 2019 - Carte MCU

custom parts:
  Wemos Lolin32lite: Wemos Lolinlite32 wifi and blue tooth board based on the ESP-32 cpu, digital I/Os 19, analog inputs 6, clock 240mhz, Flash 4Mbytes, lipo battery charger (500ma connection broken out on breadboard but not pcb), usb.
