# Fritzing sketch Esp_Mad_V1.1_CarteMPU (saved by Fritzing 0.9.3b)
circuit board: 3.5cm x 5.5cm

parts:
  MPU_6050 = MPU-6050 Board GY-521 [form="♀ (female)" package=THT]
  TP1 = TP4056 [chip_label=TP4056 package="DIP (Dual Inline) [THT]"]  # not connected
  J1 = female pin header, 4 pins [form="♀ (female)"]

nets:
  N1: MPU_6050.pin1, J1.pin4
  N2: MPU_6050.pin2, J1.pin3
  N3: MPU_6050.pin3, J1.pin2
  N4: MPU_6050.pin4, J1.pin1

notes:
  ESP-MAD V1.1 - Aneg 2019 - Carte MPU
  VCC
  GND
  SCL
  SDA

custom parts:
  MPU-6050 Board GY-521: Acelerometro y Giroscopio MPU-6050 Board GY-521
  TP4056: A DIP stand-in part for whatever IC you want. With 6 pins on a 300mil dual inline package (DIP) footprint.
