# Fritzing sketch Esp_Mad_V1.2_CarteMPU (saved by Fritzing 0.9.3b)
circuit board: 3.5cm x 3.8cm

parts:
  MPU_6050 = MPU-6050 Board GY-521 [form="♀ (female)" package=THT]
  TP1 = TP4056 [chip_label=TP4056 package="DIP (Dual Inline) [THT]"]  # not connected
  SDA/SCL/GND/VCC = female pin header, 4 pins [form="♀ (female)"]

nets:
  N1: MPU_6050.pin1, SDA/SCL/GND/VCC.pin4
  N2: MPU_6050.pin2, SDA/SCL/GND/VCC.pin3
  N3: MPU_6050.pin3, SDA/SCL/GND/VCC.pin2
  N4: MPU_6050.pin4, SDA/SCL/GND/VCC.pin1

notes:
  ESP-MAD V1.2
  SCL
  ANEG 2019

custom parts:
  MPU-6050 Board GY-521: Acelerometro y Giroscopio MPU-6050 Board GY-521
  TP4056: A DIP stand-in part for whatever IC you want. With 6 pins on a 300mil dual inline package (DIP) footprint.
