# Fritzing sketch Esp_Mad_V1.3_CarteMPU (saved by Fritzing 0.9.3b)
circuit board: 3.9cm x 3.9cm

parts:
  MPU_6050 = MPU-6050 Board GY-521 [form="♀ (female)" package=THT]
  TP1 = TP4056 [chip_label=TP4056 package="DIP (Dual Inline) [THT]"]  # not connected
  SDA/SCL/GND/VCC = female pin header, 4 pins [form="♀ (female)"]
  R1 = Resistor [tolerance=±5% resistance=680 package=THT]
  LED1 = LED - 5mm [color="Red (633nm)" package="5 mm [THT]"]
  P13 = female pin header, 1 pin [form="♀ (female)"]

nets:
  N1: MPU_6050.pin1, SDA/SCL/GND/VCC.pin4
  N2: MPU_6050.pin2, SDA/SCL/GND/VCC.pin3, LED1.cathode
  N3: MPU_6050.pin3, SDA/SCL/GND/VCC.pin2
  N4: MPU_6050.pin4, SDA/SCL/GND/VCC.pin1
  N5: R1.Pin_0, LED1.anode
  N6: R1.Pin_1, P13.pin1

notes:
  ESP-MAD V1.3
  SCL
  ANEG 2019

custom parts:
  MPU-6050 Board GY-521: Acelerometro y Giroscopio MPU-6050 Board GY-521
  TP4056: A DIP stand-in part for whatever IC you want. With 6 pins on a 300mil dual inline package (DIP) footprint.
